# Fritzing sketch Cartesian Barometer (saved by Fritzing 1.0.2b)
breadboards: 1

parts:
  A1 = Teensy 4.0
  A2 = GC9A01 round lcd
  Part1 = Adafruit BMP390 [part_number="Adafruit #4816"]
  LCD1 = 2.8" SPI TFT Module [part_number=MSP2807]
  R2 = TRIMPOT [maximum_resistance=10kΩ knob_status=50% power=0.5W package=3386u]
  C1 = Electrolytic Capacitor [capacitance=1µF voltage=35V package="100 mil [THT, electrolytic]"]

nets:
  N1: A1.pin_1, A1.pin_17, A1.pin_32, A2.Pin_6, Part1.GND, LCD1.pin2, R2.CW, C1.+
  N2: A1.pin_6, A2.Pin_1
  N3: A1.pin_7, LCD1.pin4
  N4: A1.pin_8, LCD1.pin5
  N5: A1.pin_9, A2.Pin_2
  N6: A1.pin_10, Part1.CS
  N7: A1.pin_11, A2.Pin_3
  N8: A1.pin_12, LCD1.pin3
  N9: A1.pin_13, A2.Pin_4, Part1.SDI/SDA, LCD1.pin6
  N10: A1.pin_14, Part1.SDO/ADR
  N11: A1.pin_20, A2.Pin_5, Part1.SCK/SCL, LCD1.pin7
  N12: A1.pin_21, R2.WIPER
  N13: A1.pin_31, LCD1.pin1
  N14: A1.pin33, Part1.VCC
  N15: LCD1.pin8, C1.-

custom parts:
  Teensy 4.0: The Teensy is a complete USB-based microcontoller development system, in a very small footprint, capable of implementing many types of projects. All programming is done via the USB port. No special programmer is needed, only a standard micro-USB cable and a PC or Macintosh with a USB port. (Oct 2023 added the VBUS pad at user request.)
  GC9A01 round lcd: IPS TFT display round 1.28″ 240×240 GC9A01 controller. Mar 2025 fix pcb pin with fill #ffffff instead of none. Casuses problem in etchable pcb images (pad with no hole.)
  Adafruit BMP390: Bosch has been a leader in barometric pressure sensors, from the BMP085. BMP180, BMP280, BMP388... now we've got the next generation, the Adafruit BMP390 Precision Barometric Pressure and Altimeter Breakout. As you would expect, this sensor is similar to its earlier versions but even better. The BMP390 has better precision than ever, which makes it excellent for environmental sensing or as a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
  2.8" SPI TFT Module: A generic 2.8 inch LCD TFT 320x240 display with touchscreen and SD card slot. Uses the ILI9341 controller, like the Adafruit displays of this size uses.
